// Logisim project Arq_Comp.circ as structural Verilog: 1 circuit, main circuit main
module main (
  input  A,
  input  B,
  input  C,
  input  D,
  input  E,
  output S
);

  wire and_1_out, and_2_out, and_3_out, and_4_out, and_5_out, and_6_out, and_7_out, and_8_out, and_9_out,
       and_10_out, and_11_out, and_12_out, and_13_out, and_14_out, and_15_out, and_16_out, and_17_out,
       and_18_out, and_19_out, and_20_out, and_21_out, and_22_out, and_23_out, and_24_out, not_1_out,
       not_2_out, not_3_out, not_4_out, not_5_out, not_6_out, not_7_out, not_8_out, not_9_out, not_10_out,
       not_11_out, not_12_out, not_13_out, not_14_out, not_15_out, not_16_out, not_17_out, not_18_out,
       not_19_out, not_20_out, not_21_out, not_22_out, not_23_out, not_24_out, not_25_out, not_26_out,
       not_27_out, not_28_out, not_29_out, not_30_out, not_31_out, not_32_out, not_33_out, not_34_out,
       not_35_out, not_36_out, not_37_out, not_38_out, not_39_out, not_40_out, not_41_out, not_42_out,
       not_43_out, not_44_out, not_45_out, not_46_out, not_47_out, not_48_out, not_49_out, not_50_out,
       not_51_out, not_52_out, not_53_out, not_54_out, not_55_out, not_56_out, not_57_out, not_58_out,
       not_59_out, not_60_out;

  not not_1 (not_1_out, A);
  not not_2 (not_2_out, B);
  not not_3 (not_3_out, C);
  not not_4 (not_4_out, D);
  not not_5 (not_5_out, E);
  not not_6 (not_6_out, A);
  not not_7 (not_7_out, B);
  not not_8 (not_8_out, C);
  not not_9 (not_9_out, D);
  not not_10 (not_10_out, A);
  not not_11 (not_11_out, B);
  not not_12 (not_12_out, D);
  not not_13 (not_13_out, E);
  not not_14 (not_14_out, A);
  not not_15 (not_15_out, B);
  not not_16 (not_16_out, D);
  not not_17 (not_17_out, A);
  not not_18 (not_18_out, C);
  not not_19 (not_19_out, D);
  not not_20 (not_20_out, E);
  not not_21 (not_21_out, A);
  not not_22 (not_22_out, C);
  not not_23 (not_23_out, D);
  not not_24 (not_24_out, A);
  not not_25 (not_25_out, C);
  not not_26 (not_26_out, E);
  not not_27 (not_27_out, A);
  not not_28 (not_28_out, C);
  not not_29 (not_29_out, A);
  not not_30 (not_30_out, D);
  not not_31 (not_31_out, E);
  not not_32 (not_32_out, A);
  not not_33 (not_33_out, D);
  not not_34 (not_34_out, A);
  not not_35 (not_35_out, E);
  not not_36 (not_36_out, A);
  not not_37 (not_37_out, B);
  not not_38 (not_38_out, C);
  not not_39 (not_39_out, D);
  not not_40 (not_40_out, E);
  not not_41 (not_41_out, B);
  not not_42 (not_42_out, C);
  not not_43 (not_43_out, D);
  not not_44 (not_44_out, B);
  not not_45 (not_45_out, D);
  not not_46 (not_46_out, E);
  not not_47 (not_47_out, B);
  not not_48 (not_48_out, D);
  not not_49 (not_49_out, C);
  not not_50 (not_50_out, D);
  not not_51 (not_51_out, E);
  not not_52 (not_52_out, C);
  not not_53 (not_53_out, D);
  not not_54 (not_54_out, C);
  not not_55 (not_55_out, E);
  not not_56 (not_56_out, C);
  not not_57 (not_57_out, D);
  not not_58 (not_58_out, E);
  not not_59 (not_59_out, D);
  not not_60 (not_60_out, E);
  and and_1 (and_1_out, not_1_out, not_2_out, not_3_out, not_4_out, not_5_out);
  and and_2 (and_2_out, not_6_out, not_7_out, not_8_out, not_9_out, E);
  and and_3 (and_3_out, not_10_out, not_11_out, C, not_12_out, not_13_out);
  and and_4 (and_4_out, not_14_out, not_15_out, C, not_16_out, E);
  and and_5 (and_5_out, not_17_out, B, not_18_out, not_19_out, not_20_out);
  and and_6 (and_6_out, not_21_out, B, not_22_out, not_23_out, E);
  and and_7 (and_7_out, not_24_out, B, not_25_out, D, not_26_out);
  and and_8 (and_8_out, not_27_out, B, not_28_out, D, E);
  and and_9 (and_9_out, not_29_out, B, C, not_30_out, not_31_out);
  and and_10 (and_10_out, not_32_out, B, C, not_33_out, E);
  and and_11 (and_11_out, not_34_out, B, C, D, not_35_out);
  and and_12 (and_12_out, not_36_out, B, C, D, E);
  and and_13 (and_13_out, A, not_37_out, not_38_out, not_39_out, not_40_out);
  and and_14 (and_14_out, A, not_41_out, not_42_out, not_43_out, E);
  and and_15 (and_15_out, A, not_44_out, C, not_45_out, not_46_out);
  and and_16 (and_16_out, A, not_47_out, C, not_48_out, E);
  and and_17 (and_17_out, A, B, not_49_out, not_50_out, not_51_out);
  and and_18 (and_18_out, A, B, not_52_out, not_53_out, E);
  and and_19 (and_19_out, A, B, not_54_out, D, not_55_out);
  and and_20 (and_20_out, A, B, not_56_out, D, E);
  and and_21 (and_21_out, A, B, C, not_57_out, not_58_out);
  and and_22 (and_22_out, A, B, C, not_59_out, E);
  and and_23 (and_23_out, A, B, C, D, not_60_out);
  and and_24 (and_24_out, A, B, C, D, E);
  or or_1 (S, and_1_out, and_2_out, and_3_out, and_4_out, and_5_out, and_6_out, and_7_out, and_8_out, and_9_out, and_10_out, and_11_out, and_12_out, and_13_out, and_14_out, and_15_out, and_16_out, and_17_out, and_18_out, and_19_out, and_20_out, and_21_out, and_22_out, and_23_out, and_24_out);
endmodule
