// Logisim project desafiobooleano.circ as structural Verilog: 1 circuit, main circuit main
module main (
  input  A,
  input  B,
  input  C,
  input  D,
  input  E,
  output out_6
);

  wire S1_out, S2_out, S3_out, S4_out, S5_out, S6_out, S7_out, S8_out, S9_out, S10_out, S11_out, S12_out;

  and S1 (S1_out, A, C, E);
  xor S2 (S2_out, B, D);
  not S3 (S3_out, D);
  not S4 (S4_out, S1_out);
  or S6 (S6_out, S4_out, S2_out);
  and S5 (S5_out, S3_out, C, A);
  and S7 (S7_out, S2_out, D);
  and S8 (S8_out, S6_out, S7_out);
  nand S9 (S9_out, S7_out, S5_out);
  or S10 (S10_out, S7_out, S9_out, E);
  not S11 (S11_out, S10_out);
  not S13 (out_6, S12_out);
  or S12 (S12_out, S8_out, S11_out);
endmodule
